# Fritzing sketch schematic (saved by Fritzing 0.9.3b)

parts:
  Part2 = Arduino Pro Mini v13
  R1 = Resistor [tolerance=±5% resistance=1k package=THT]  # not connected
  R2 = Resistor [tolerance=±5% resistance=1k package=THT]  # not connected
  R3 = Resistor [tolerance=±5% resistance=1k package=THT]  # not connected
  R4 = Resistor [tolerance=±5% resistance=1k package=THT]  # not connected
  R5 = Resistor [tolerance=±5% resistance=1k package=THT]  # not connected
  C1 = Electrolytic Capacitor [capacitance=100µF voltage=50V package="200 mil [THT, electrolytic]"]

nets:
  N1: Part2.GND, C1.-
  N2: Part2.D12/MISO, C1.+

notes:
  Charging ►
  ◄ Measuring
  ◄ Discharging
  To Computer
  ▲ ▲ ▲ ▲
